# Fritzing sketch main (saved by Fritzing 0.9.3b)
breadboards: 1

parts:
  XTAL1 = Crystal [frequency="16 Mhz" package=THT]
  Raspberry_Pi_2 = Raspberry Pi 2
  M2 = male pin header, 2 pins [form="♂ (male)"]
  M3 = male pin header, 2 pins [form="♂ (male)"]
  M4 = male pin header, 2 pins [form="♂ (male)"]
  M1 = male pin header, 2 pins [form="♂ (male)"]
  A2 = male pin header, 3 pins [form="♂ (male)"]
  A1 = male pin header, 3 pins [form="♂ (male)"]
  A0 = male pin header, 3 pins [form="♂ (male)"]
  Disp = male pin header, 3 pins [form="♂ (male)"]
  Q2 = MOSFET-NCHANNEL [package=to-92]
  Q3 = MOSFET-NCHANNEL [package=to-92]
  Q1 = MOSFET-NCHANNEL [package=to-92]
  GPS = mystery part, 9 pins [chip_label=GPS]
  REG1 = mystery part, 4 pins [chip_label="5V CRIT" part_number=D24V5F5]
  REG2 = mystery part, 4 pins [chip_label=3.3V part_number=D24V5F3]
  Q5 = MOSFET-NCHANNEL [package=to-92]
  PWR = Screw terminal - 2 pins [package=THT]
  Q4 = MOSFET-NCHANNEL [package=to-92]
  REG3 = mystery part, 5 pins [chip_label=5V part_number=D24V22F5]
  Port_1 = Interconnect Port [form="♂ (shrouded male)" package=THT]
  Port_2 = Interconnect Port [form="♂ (shrouded male)" package=THT]
  Port_3 = Interconnect Port [form="♂ (shrouded male)" package=THT]
  Port_4 = Interconnect Port [form="♂ (shrouded male)" package=THT]
  U1 = ATmega328 [package=tqfp]
  C3 = Ceramic Capacitor [capacitance=100nF package="0805 [SMD, multilayer]"]
  C4 = Ceramic Capacitor [capacitance=100nF package="0805 [SMD, multilayer]"]
  R3 = Resistor [tolerance=±1% resistance=10k package="0805 [SMD]"]
  C2 = Ceramic Capacitor [capacitance=22pF package="0805 [SMD, multilayer]"]
  C1 = Ceramic Capacitor [capacitance=22pF package="0805 [SMD, multilayer]"]
  R4 = Resistor [tolerance=±1% resistance=10k package="0805 [SMD]"]
  R5 = Resistor [tolerance=±1% resistance=10k package="0805 [SMD]"]
  R6 = Resistor [tolerance=±1% resistance=10k package="0805 [SMD]"]
  R7 = Resistor [tolerance=±1% resistance=10k package="0805 [SMD]"]
  R8 = Resistor [tolerance=±1% resistance=100k package="0805 [SMD]"]
  R10 = Resistor [tolerance=±1% resistance=100k package="0805 [SMD]"]
  R9 = Resistor [tolerance=±1% resistance=100k package="0805 [SMD]"]
  R2 = Resistor [tolerance=±1% resistance=100k package="0805 [SMD]"]
  R1 = Resistor [tolerance=±1% resistance=10k package="0805 [SMD]"]
  IC1 = TSSOP20 [chip_label=74LVC244 package=TSSOP]

nets:
  N1: XTAL1.pin_0, U1.PB7(XTAL2_TOSC2), C1.0
  N2: XTAL1.pin_1, U1.PB6(XTAL1_TOSC1), C2.0
  3.3V_SDA: Raspberry_Pi_2.GPIO2, Q2.S, R4.Pin_0
  3.3V_SCL: Raspberry_Pi_2.GPIO3, Q3.S, R5.Pin_0
  PI_MOSI: Raspberry_Pi_2.GPIO10, IC1.6
  PI_MISO: Raspberry_Pi_2.GPIO9, IC1.12
  PI_SCK: Raspberry_Pi_2.GPIO11, IC1.4
  GND: Raspberry_Pi_2.GND, A2.pin3, A1.pin3, A0.pin3, Disp.pin3, Q1.S, GPS.pin7, REG1.pin3, REG2.pin3, PWR.pin2, REG3.pin4, Port_1.GND, Port_2.GND, Port_3.GND, Port_4.GND, U1.GND, U1.AGND, C3.0, C4.1, C2.1, C1.1, R8.Pin_1, R10.Pin_0, R2.Pin_0, IC1.10, IC1.11, IC1.13, IC1.15, IC1.17
  N3: Raspberry_Pi_2.GPIO26, GPS.pin2
  PI_CE0: Raspberry_Pi_2.GPIO8, R1.Pin_0, IC1.1
  N4: Raspberry_Pi_2.GPIO15, GPS.pin5
  N5: Raspberry_Pi_2.GPIO14, GPS.pin6
  5V: Raspberry_Pi_2.5V, A2.pin2, A1.pin2, A0.pin2, Disp.pin2, REG2.pin2, Q4.D, REG3.pin5, Port_1.5V, Port_2.5V, Port_3.5V, Port_4.5V, R6.Pin_1, R7.Pin_1
  AVR_D4: M2.pin1, U1.PD4(XCK_T0)
  PWM1: M2.pin2, U1.PD5(T1)
  AVR_D7: M3.pin1, U1.PD7(AIN1)
  PWM2: M3.pin2, U1.PD6(AIN0)
  AVR_D8: M4.pin1, U1.PB0(ICP)
  PWM3: M4.pin2, U1.PB1(OC1A)
  AVR_D2: M1.pin1, U1.PD2(INT0)
  PWM0: M1.pin2, U1.PD3(INT1)
  ADC2: A2.pin1, U1.PC2(ADC2)
  ADC1: A1.pin1, U1.PC1(ADC1)
  ADC0: A0.pin1, U1.PC0(ADC0)
  N6: Disp.pin1, U1.PB2(SS_OC1B)
  5V_SDA: Q2.D, Port_1.SDA, Port_2.SDA, Port_3.SDA, Port_4.SDA, U1.PC4(ADC4_SDA), R7.Pin_0
  3.3V: Q2.G, Q3.G, GPS.pin1, REG2.pin4, Port_1.3.3V, Port_2.3.3V, Port_3.3.3V, Port_4.3.3V, R4.Pin_1, R5.Pin_1, R1.Pin_1, IC1.19, IC1.20
  5V_SCL: Q3.D, Port_1.SCL, Port_2.SCL, Port_3.SCL, Port_4.SCL, U1.PC5(ADC5_SCL), R6.Pin_0
  AVR_RST: Q1.D, U1.PC6(_RESET), R3.Pin_1
  N7: Q1.G, R2.Pin_1, IC1.18
  VIN: REG1.pin2, PWR.pin1, REG3.pin3, R9.Pin_1
  5V CRIT: REG1.pin4, Port_1.5V_CRIT, Port_2.5V_CRIT, Port_3.5V_CRIT, Port_4.5V_CRIT, U1.VCC, U1.AVCC, C3.1, C4.0, R3.Pin_0
  N8: Q5.D, REG3.pin2
  N9: Q5.S, R8.Pin_0
  SHDN: Q5.G, U1.PD0(RXD)
  PG: Q4.S, U1.PD1(TXD)
  N10: Q4.G, REG3.pin1
  AVR_MOSI: U1.PB3(MOSI_OC2)
  AVR_MISO: U1.PB4(MISO), IC1.8
  AVR_SCK: U1.PB5(SCK)
  ADC3: U1.PC3(ADC3), R10.Pin_1, R9.Pin_0

notes:
  I2C Level Shifter
  Raspberry Pi Header
  Atmel ATMEGA 328p
  ATMEGA Programmer
  ADC Header
  Expansion Ports
  Motors
  5V
  G
  A
  Rx
  E
  Pathfinder v3.0
  Frontier Robotics ©2016
  M
  +
  -
  GND
  RX
  TX
  EN
  3.3V
  CRIT
  PG
  VIN

custom parts:
  MOSFET-NCHANNEL: Generic NMOS footprint
  Interconnect Port: 6 pin shrouded header for board interconnection.
