# Fritzing sketch navigator (saved by Fritzing 0.9.2b)
breadboards: 1

parts:
  U1 = atmega328 [package=dip]
  XTAL1 = Crystal [frequency="16 Mhz" package=THT]
  IC1 = IC, DIP package, 20 pins [chip_label=74LVC244]
  GPS1 = female pin header, 9 pins [form="♀ (female)"]
  Raspberry_Pi_2 = Raspberry Pi 2

nets:
  N1: U1.XLAT1, XTAL1.pin_1
  N2: U1.XLAT2, XTAL1.pin_0
  3V3: IC1.pin20, GPS1.pin1, Raspberry_Pi_2.3v3, Raspberry_Pi_2.3V3
  N3: GPS1.pin5, Raspberry_Pi_2.GPIO15
  N4: GPS1.pin6, Raspberry_Pi_2.GPIO14
  GND: GPS1.pin7, Raspberry_Pi_2.GND

notes:
  3.3V
  EN
  VBAT
  FIX
  TX
  RX
  GND
  VIN
  PPS
